// Logisim project ALU.circ as structural Verilog: 1 circuit, main circuit ALU
module ALU (
  input  Cin,
  input  [7:0] A,
  input  [7:0] B,
  input  [2:0] Operation,
  output [3:0] Flags,
  output [7:0] Result
);

  wire adder_1_cout, and_2_out, and_3_out, and_4_out, and_5_out, decoder_1_out0, decoder_1_out1,
       decoder_1_out2, decoder_1_out3, decoder_1_out4, decoder_1_out5, decoder_1_out6, decoder_1_out7,
       or_1_out, or_4_out, xnor_1_out, xor_3_out;
  wire [7:0] adder_1_out, and_1_out, or_2_out, xor_1_out, xor_2_out;
  wire [7:7] or_3_out;

  or or_1 (or_1_out, Cin, decoder_1_out7);
  assign xor_1_out = B ^ {8{or_3_out[7]}};  // XOR_Gate xor_1, 8 bits wide
  Adder adder_1 (.a(A), .b(xor_1_out), .out(adder_1_out), .cin(or_1_out), .cout(adder_1_cout));
  assign and_1_out = A & B;  // AND_Gate and_1, 8 bits wide
  assign or_2_out = A | B;  // OR_Gate or_2, 8 bits wide
  assign xor_2_out = A ^ B;  // XOR_Gate xor_2, 8 bits wide
  xnor xnor_1 (xnor_1_out, xor_1_out[7], A[7]);
  or or_3 (or_3_out[7], decoder_1_out1, decoder_1_out7);
  Decoder #(.select(3), .enable("false")) decoder_1 (
    .out0(decoder_1_out0), .out1(decoder_1_out1), .out2(decoder_1_out2), .out3(decoder_1_out3),
    .out4(decoder_1_out4), .out5(decoder_1_out5), .out6(decoder_1_out6), .out7(decoder_1_out7),
    .sel(Operation));
  assign {Flags[2], Result[6:0]} = or_4_out ? adder_1_out : 8'bz;  // Controlled_Buffer controlled_buffer_1
  or or_4 (or_4_out, decoder_1_out0, or_3_out[7]);
  assign {Flags[2], Result[6:0]} = decoder_1_out2 ? {A[6:0], Cin} : 8'bz;  // Controlled_Buffer controlled_buffer_2
  assign {Flags[2], Result[6:0]} = decoder_1_out3 ? {Cin, A[7:1]} : 8'bz;  // Controlled_Buffer controlled_buffer_3
  assign {Flags[2], Result[6:0]} = decoder_1_out4 ? and_1_out : 8'bz;  // Controlled_Buffer controlled_buffer_4
  assign {Flags[2], Result[6:0]} = decoder_1_out5 ? or_2_out : 8'bz;  // Controlled_Buffer controlled_buffer_5
  assign {Flags[2], Result[6:0]} = decoder_1_out6 ? xor_2_out : 8'bz;  // Controlled_Buffer controlled_buffer_6
  and and_2 (and_2_out, xnor_1_out, ~adder_1_cout);  // AND_Gate
  and and_3 (and_3_out, adder_1_cout, or_4_out);
  and and_4 (and_4_out, A[7], decoder_1_out2);
  or or_5 (Flags[0], and_3_out, and_4_out, and_5_out);
  and and_5 (and_5_out, A[0], decoder_1_out3);
  xor xor_3 (xor_3_out, xor_1_out[7], Flags[2]);
  nor nor_1 (Flags[1], Flags[2], Result[6], Result[5], Result[4], Result[2], Result[1], Result[0], Result[3]);
  and and_6 (Flags[3], and_2_out, xor_3_out);

  assign Result[7] = Flags[2];

  // Notes on the sheet:
  //   000 - ADC
  //   001 - SBC
  //   010 - SHL
  //   011 - SHR
  //   100 - AND
  //   101 - OR
  //   110 - XOR
  //   111 - CMP
  //   Overflow
  //   Negative
  //   Zero
  //   Carry
  //   O N Z C
endmodule
