// Logisim project CPU.circ as structural Verilog: 6 circuits, main circuit main
module main (
  input  in_1,
  input  in_2,
  input  in_3,
  input  in_4,
  input  in_5,
  input  in_6,
  input  in_7,
  input  in_8,
  input  in_9,
  input  in_10,
  input  [2:0] in_11,
  input  in_12,
  input  in_13,
  input  in_14,
  input  in_15,
  input  in_16,
  input  in_17,
  input  in_18,
  input  in_19,
  input  in_20,
  input  in_21,
  input  in_22,
  input  in_23,
  input  in_24,
  input  in_25,
  input  in_26,
  input  in_27,
  input  in_28,
  input  in_29,
  input  in_30,
  input  in_31,
  input  in_32,
  input  in_33,
  input  in_34,
  input  in_35,
  input  in_36,
  input  in_37,
  input  in_38
);

  wire and_1_out, and_2_out, and_3_out, Clk, Clk_t, clock_1_out, DI_nCntEna, Hadda_nOE, hm62256sel_1_load,
       hm62256sel_1_sel, MAR_nCntEna, MEM_ne, MEM_ns, nand_1_out, not_10_out, not_11_out, or_1_out,
       PC_nCntEna, romsel_1_romh, romsel_1_roml, Rst, SI_nCntEna, SP_nCntEna;
  wire [3:0] alu_1_flags, Flags;
  wire [7:0] alu_1_result, bus1_1_out_3, controlled_buffer_4_out, n8bitreg_1_dout, n8bitreg_1_dout_2,
       n8bitreg_2_dout, n8bitreg_3_dout, n8bitreg_4_dout, n8bitreg_5_dout, n8bitreg_6_dout, n8bitreg_7_dout,
       n8bitreg_7_dout_2, n8bitreg_8_dout, n8bitreg_9_dout, n16bitreg_1_dout_2, pull_resistor_1_node;
  wire [7:4] n8bitreg_9_dout_2, pull_resistor_3_node;
  wire [15:0] n16bitreg_1_dout, n16bitreg_2_dout, n16bitreg_3_dout, n16bitreg_4_dout, n16bitreg_5_dout,
       n16bitreg_5_dout_2;

  Button button_1 (.out(Rst));
  Clock clock_1 (.out(clock_1_out));
  not not_1 (SP_nCntEna, in_6);
  not not_2 (PC_nCntEna, in_12);
  not not_3 (DI_nCntEna, in_15);
  not not_4 (SI_nCntEna, in_18);
  not not_5 (MAR_nCntEna, in_21);
  not not_6 (Hadda_nOE, in_26);
  not not_7 (MEM_ne, in_36);
  not not_8 (MEM_ns, in_37);
  buf buffer_1 (Clk, clock_1_out);
  not not_9 (Clk_t, clock_1_out);
  _8bitreg u_8bitreg_1 (
    .Load(in_23), .DataIn(pull_resistor_1_node), .nCntEna(1'b1), .Reset(Rst), .Up_nDown(1'b0),
    .Enable(in_24), .Dout(n8bitreg_1_dout), .Dout_2(n8bitreg_1_dout_2));  // open: Clock, Zout
  Pull_Resistor pull_resistor_1 (.node(pull_resistor_1_node));
  _8bitreg u_8bitreg_2 (
    .Load(in_38), .DataIn(pull_resistor_1_node), .nCntEna(1'b1), .Reset(Rst), .Up_nDown(1'b0), .Enable(1'b1),
    .Dout(n8bitreg_2_dout));  // open: Clock, Dout_2, Zout
  // Probe on n8bitreg_2_dout
  // Probe on n8bitreg_1_dout
  _16bitreg u_16bitreg_1 (
    .DataIn({n16bitreg_1_dout_2, n8bitreg_1_dout_2}), .Clock(Clk_t), .Load(in_8), .nCntEna(SP_nCntEna),
    .Up_nDown(in_2), .Reset(Rst), .Enable(in_10), .Dout(n16bitreg_1_dout),
    .Dout_2({n16bitreg_1_dout_2, n8bitreg_1_dout_2}));
  // Probe on n16bitreg_1_dout
  _16bitreg u_16bitreg_2 (
    .DataIn({n16bitreg_1_dout_2, n8bitreg_1_dout_2}), .Clock(Clk_t), .Load(in_13), .nCntEna(PC_nCntEna),
    .Up_nDown(in_2), .Reset(Rst), .Enable(in_14), .Dout(n16bitreg_2_dout),
    .Dout_2({n16bitreg_1_dout_2, n8bitreg_1_dout_2}));
  // Probe on n16bitreg_2_dout
  _8bitreg u_8bitreg_3 (
    .Load(in_28), .DataIn(pull_resistor_1_node), .nCntEna(1'b1), .Reset(Rst), .Up_nDown(1'b0),
    .Enable(in_29), .Dout(n8bitreg_3_dout), .Dout_2(pull_resistor_1_node));  // open: Clock, Zout
  // Probe on n8bitreg_3_dout
  _8bitreg u_8bitreg_4 (
    .Load(in_30), .DataIn(pull_resistor_1_node), .nCntEna(1'b1), .Reset(Rst), .Up_nDown(1'b0),
    .Enable(in_31), .Dout(n8bitreg_4_dout), .Dout_2(pull_resistor_1_node));  // open: Clock, Zout
  // Probe on n8bitreg_4_dout
  // Probe on n16bitreg_3_dout
  _16bitreg u_16bitreg_3 (
    .DataIn({n16bitreg_1_dout_2, n8bitreg_1_dout_2}), .Clock(Clk_t), .Load(in_16), .nCntEna(DI_nCntEna),
    .Up_nDown(in_2), .Reset(Rst), .Enable(in_17), .Dout(n16bitreg_3_dout),
    .Dout_2({n16bitreg_1_dout_2, n8bitreg_1_dout_2}));
  _8bitreg u_8bitreg_5 (
    .Load(in_32), .DataIn(pull_resistor_1_node), .nCntEna(1'b1), .Reset(Rst), .Up_nDown(1'b0),
    .Enable(in_33), .Dout(n8bitreg_5_dout), .Dout_2(pull_resistor_1_node));  // open: Clock, Zout
  _16bitreg u_16bitreg_4 (
    .DataIn({n16bitreg_1_dout_2, n8bitreg_1_dout_2}), .Clock(Clk_t), .Load(in_19), .nCntEna(SI_nCntEna),
    .Up_nDown(in_2), .Reset(Rst), .Enable(in_20), .Dout(n16bitreg_4_dout),
    .Dout_2({n16bitreg_1_dout_2, n8bitreg_1_dout_2}));
  // Probe on n8bitreg_5_dout
  // Probe on n16bitreg_4_dout
  Pull_Resistor pull_resistor_2 (.node({n16bitreg_1_dout_2, n8bitreg_1_dout_2}));
  _8bitreg u_8bitreg_6 (
    .Load(in_34), .DataIn(pull_resistor_1_node), .nCntEna(1'b1), .Reset(Rst), .Up_nDown(1'b0),
    .Enable(in_35), .Dout(n8bitreg_6_dout), .Dout_2(pull_resistor_1_node));  // open: Clock, Zout
  // Probe on n8bitreg_6_dout
  and and_1 (and_1_out, in_25, ~Hadda_nOE);  // AND_Gate
  assign pull_resistor_1_node = and_1_out ? n16bitreg_1_dout_2 : 8'bz;  // Controlled_Buffer controlled_buffer_1
  assign n16bitreg_1_dout_2 = and_2_out ? pull_resistor_1_node : 8'bz;  // Controlled_Buffer controlled_buffer_2
  assign pull_resistor_1_node = in_27 ? n8bitreg_1_dout_2 : 8'bz;  // Controlled_Buffer controlled_buffer_3
  // Probe on pull_resistor_1_node
  _8bitreg u_8bitreg_7 (
    .Load(in_5), .DataIn(pull_resistor_1_node), .nCntEna(1'b1), .Reset(Rst), .Up_nDown(1'b0), .Enable(1'b1),
    .Dout(n8bitreg_7_dout), .Dout_2(n8bitreg_7_dout_2));  // open: Clock, Zout
  // Probe on n8bitreg_7_dout
  Bus1 bus1_1 (.in_1(n8bitreg_7_dout_2), .in_2(in_4), .out_3(bus1_1_out_3));
  and and_2 (and_2_out, ~in_25, ~Hadda_nOE);  // AND_Gate
  // Probe on {n16bitreg_1_dout_2, n8bitreg_1_dout_2}
  and and_3 (and_3_out, ~in_4, Flags[0]);  // AND_Gate
  ALU alu_1 (
    .Cin(and_3_out), .A(pull_resistor_1_node), .B(bus1_1_out_3), .Operation(in_11), .Flags(alu_1_flags),
    .Result(alu_1_result));
  Pull_Resistor pull_resistor_3 (.node({pull_resistor_3_node, alu_1_flags}));
  _8bitreg u_8bitreg_8 (
    .Load(in_7), .DataIn(alu_1_result), .nCntEna(1'b1), .Reset(Rst), .Up_nDown(1'b0), .Enable(in_9),
    .Dout(n8bitreg_8_dout), .Dout_2(pull_resistor_1_node));  // open: Clock, Zout
  _16bitreg u_16bitreg_5 (
    .DataIn({n16bitreg_1_dout_2, n8bitreg_1_dout_2}), .Clock(Clk_t), .Load(in_22), .nCntEna(MAR_nCntEna),
    .Up_nDown(in_2), .Reset(Rst), .Enable(1'b1), .Dout(n16bitreg_5_dout), .Dout_2(n16bitreg_5_dout_2));
  // Probe on n16bitreg_5_dout
  assign controlled_buffer_4_out = in_1 ? pull_resistor_1_node : 8'bz;  // Controlled_Buffer controlled_buffer_4
  assign controlled_buffer_4_out = in_7 ? {pull_resistor_3_node, alu_1_flags} : 8'bz;  // Controlled_Buffer controlled_buffer_5
  or or_1 (or_1_out, in_1, in_7);
  // Probe on n8bitreg_8_dout
  _8bitreg u_8bitreg_9 (
    .Load(or_1_out), .DataIn(controlled_buffer_4_out), .nCntEna(1'b1), .Reset(Rst), .Up_nDown(1'b0),
    .Enable(1'b1), .Dout(n8bitreg_9_dout), .Dout_2({n8bitreg_9_dout_2, Flags}));  // open: Clock, Zout
  // Probe on n8bitreg_9_dout
  assign pull_resistor_1_node = in_3 ? {n8bitreg_9_dout_2, Flags} : 8'bz;  // Controlled_Buffer controlled_buffer_6
  nand nand_1 (nand_1_out, n16bitreg_5_dout_2[15], Clk);
  ROMsel romsel_1 (.MEM_ne(MEM_ne), .Addr(n16bitreg_5_dout_2), .ROMh(romsel_1_romh), .ROMl(romsel_1_roml));
  HM62256sel hm62256sel_1 (
    .nWE(MEM_ns), .nCE(nand_1_out), .nOE(MEM_ne), .Sel(hm62256sel_1_sel), .Load(hm62256sel_1_load));
  not not_10 (not_10_out, romsel_1_romh);
  not not_11 (not_11_out, romsel_1_roml);
  RAM #(.addrWidth(15), .bus("asynch")) ram_1 (
    .addr(n16bitreg_5_dout_2[14:0]), .data(pull_resistor_1_node), .sel(hm62256sel_1_sel),
    .ld(hm62256sel_1_load));  // open: clr
  ROM #(.addrWidth(13)) rom_1 (.addr(n16bitreg_5_dout_2[12:0]), .data(pull_resistor_1_node), .sel(not_10_out));
  ROM #(.addrWidth(13)) rom_2 (.addr(n16bitreg_5_dout_2[12:0]), .data(pull_resistor_1_node), .sel(not_11_out));

  // Other names for the same wires on the sheet: ACCena = in_9; ACCload = in_7; ALUop[2:0] = in_11; Bus1 = in_4;
  //   DIena = in_17; DIload = in_16; Fena = in_3; Fload = in_1; Had_nda = in_25; IRload = in_38; LaddaOE = in_27;
  //   lTMPena = in_24; lTMPload = in_23; MARload = in_22; PCena = in_14; PCload = in_13; RAena = in_29;
  //   RAload = in_28; RBena = in_31; RBload = in_30; RCena = in_33; RCload = in_32; RDena = in_35; RDload = in_34;
  //   SIena = in_20; SIload = in_19; SPena = in_10; SPload = in_8; TMPload = in_5; U_nD = in_2

  // Notes on the sheet:
  //   lTMP
  //   IR
  //   SP
  //   PC
  //   RA
  //   RB
  //   DI
  //   RC
  //   SI
  //   RD
  //   TMP
  //   ACC
  //   MAR
  //   F
endmodule

module _8bitreg (
  input  Load,
  input  Clock,
  input  [7:0] DataIn,
  input  nCntEna,
  input  Reset,
  input  Up_nDown,
  input  Enable,
  output Zout,
  output [7:0] Dout,
  output [7:0] Dout_2
);

  wire cd4516be_1_ncarryout;

  CD4516BE cd4516be_1 (
    .P0(DataIn[0]), .P1(DataIn[1]), .P2(DataIn[2]), .P3(DataIn[3]), .Reset(Reset), .Preset_Enable(Load),
    .Clock(Clock), .nCarryOut(cd4516be_1_ncarryout), .nCarryIn(nCntEna), .Up_Down(Up_nDown), .Q0(Dout[0]),
    .Q1(Dout[1]), .Q2(Dout[2]), .Q3(Dout[3]));  // open: VCC, VSS
  CD4516BE cd4516be_2 (
    .P0(DataIn[4]), .P1(DataIn[5]), .P2(DataIn[6]), .P3(DataIn[7]), .Reset(Reset), .Preset_Enable(Load),
    .Clock(Clock), .nCarryIn(cd4516be_1_ncarryout), .Up_Down(Up_nDown), .Q0(Dout[4]), .Q1(Dout[5]),
    .Q2(Dout[6]), .Q3(Dout[7]));  // open: nCarryOut, VCC, VSS
  nor nor_1 (Zout, Dout[7], Dout[6], Dout[5], Dout[4], Dout[3], Dout[2], Dout[1], Dout[0]);
  assign Dout_2 = Enable ? Dout : 8'bz;  // Controlled_Buffer controlled_buffer_1

  // Notes on the sheet:
  //   Dout_2: pull=down
  //   74HC4078
endmodule

module _16bitreg (
  input  [15:0] DataIn,
  input  Load,
  input  Clock,
  input  nCntEna,
  input  Up_nDown,
  input  Reset,
  input  Enable,
  output [15:0] Dout,
  output [15:0] Dout_2
);

  wire cd4516be_1_ncarryout, cd4516be_2_ncarryout, cd4516be_3_ncarryout;

  CD4516BE cd4516be_1 (
    .P0(DataIn[0]), .P1(DataIn[1]), .P2(DataIn[2]), .P3(DataIn[3]), .Reset(Reset), .Preset_Enable(Load),
    .Clock(Clock), .nCarryOut(cd4516be_1_ncarryout), .nCarryIn(nCntEna), .Up_Down(Up_nDown), .Q0(Dout[0]),
    .Q1(Dout[1]), .Q2(Dout[2]), .Q3(Dout[3]));  // open: VCC, VSS
  CD4516BE cd4516be_2 (
    .P0(DataIn[4]), .P1(DataIn[5]), .P2(DataIn[6]), .P3(DataIn[7]), .Reset(Reset), .Preset_Enable(Load),
    .Clock(Clock), .nCarryOut(cd4516be_2_ncarryout), .nCarryIn(cd4516be_1_ncarryout), .Up_Down(Up_nDown),
    .Q0(Dout[4]), .Q1(Dout[5]), .Q2(Dout[6]), .Q3(Dout[7]));  // open: VCC, VSS
  CD4516BE cd4516be_3 (
    .P0(DataIn[8]), .P1(DataIn[9]), .P2(DataIn[10]), .P3(DataIn[11]), .Reset(Reset), .Preset_Enable(Load),
    .Clock(Clock), .nCarryOut(cd4516be_3_ncarryout), .nCarryIn(cd4516be_2_ncarryout), .Up_Down(Up_nDown),
    .Q0(Dout[8]), .Q1(Dout[9]), .Q2(Dout[10]), .Q3(Dout[11]));  // open: VCC, VSS
  CD4516BE cd4516be_4 (
    .P0(DataIn[12]), .P1(DataIn[13]), .P2(DataIn[14]), .P3(DataIn[15]), .Reset(Reset), .Preset_Enable(Load),
    .Clock(Clock), .nCarryIn(cd4516be_3_ncarryout), .Up_Down(Up_nDown), .Q0(Dout[12]), .Q1(Dout[13]),
    .Q2(Dout[14]), .Q3(Dout[15]));  // open: nCarryOut, VCC, VSS
  assign Dout_2 = Enable ? Dout : 16'bz;  // Controlled_Buffer controlled_buffer_1

  // Notes on the sheet:
  //   Dout_2: pull=down
endmodule

module HM62256sel (
  input  nWE,
  input  nCE,
  input  nOE,
  output Sel,
  output Load
);

  wire nor_1_out;

  nor nor_1 (nor_1_out, nWE, nCE);
  nor nor_2 (Load, nCE, nOE);
  or or_1 (Sel, nor_1_out, Load);

  // Notes on the sheet:
  //   !WE
  //   !CE
  //   !OE
endmodule

module ROMsel (
  input  MEM_ne,
  input  [15:0] Addr,
  output ROMh,
  output ROMl
);

  wire and_1_out, and_2_out, and_3_out, not_1_out, not_2_out, not_3_out, not_4_out;

  not not_1 (not_1_out, MEM_ne);
  not not_2 (not_2_out, Addr[13]);
  not not_3 (not_3_out, Addr[14]);
  not not_4 (not_4_out, Addr[15]);
  and and_1 (and_1_out, not_3_out, not_4_out);
  and and_2 (and_2_out, Addr[13], and_1_out);
  and and_3 (and_3_out, not_2_out, and_1_out);
  nand nand_1 (ROMh, not_1_out, and_2_out);
  nand nand_2 (ROMl, not_1_out, and_3_out);
endmodule

module Bus1 (
  input  [7:0] in_1,
  input  in_2,
  output [7:0] out_3
);

  wire not_1_out;

  not not_1 (not_1_out, in_2);
  or or_1 (out_3[0], in_1[0], in_2);
  and and_1 (out_3[1], in_1[1], not_1_out);
  and and_2 (out_3[2], in_1[2], not_1_out);
  and and_3 (out_3[3], in_1[3], not_1_out);
  and and_4 (out_3[4], in_1[4], not_1_out);
  and and_5 (out_3[5], in_1[5], not_1_out);
  and and_6 (out_3[6], in_1[6], not_1_out);
  and and_7 (out_3[7], in_1[7], not_1_out);
endmodule
